# Fritzing sketch Projeto_Pivo_Irrigação (saved by Fritzing 0.9.3b)
breadboards: 2

parts:
  LED2 = LED - 5mm [color="Red (633nm)" part_number=9 package="5 mm [THT]"]
  Componente1 = Arduino Uno (Rev3) [part_number=1]
  R1 = Resistor [tolerance=±5% resistance=220 part_number=11 package=THT]
  R2 = Resistor [tolerance=±5% resistance=220 part_number=10 package=THT]
  LED3 = LED - 5mm [color="Green (555nm)" part_number=7 package="5 mm [THT]"]
  LED1 = smd LED [color="Yellow (592nm)" part_number=8 package="0603 [SMD]"]
  R3 = Resistor [tolerance=±5% resistance=220 part_number=12 package=THT]
  LCD1 = LCD screen [part_number=6]
  S2 = Pushbutton [package="[SMD]"]
  U2 = ESP8266 WiFi Module [part_number=ESP8266]
  LCM1602_IIC2 = LCM1602 IIC [part_number="LCM1602 IIC" chip_label="LCM1602 IIC" package="DIP (Dual Inline) [THT]"]
  Tiny_RTC2 = Tiny RTC
  Part6 = FC-28 Soil Hygrometer Module
  M1 = DC Motor  # not connected
  VALVE2 = Plastic Solenoid Valve
  Part7 = FC-28 Soil Hygrometer Module - Probe
  S3 = Pushbutton [package="[THT]"]
  S4 = Pushbutton [package="[THT]"]
  Power_plug1 = Power plug
  KY-2 = Keyes Relay [package=THT]

nets:
  N1: LED2.cathode, R2.Pin_0
  N2: LED2.anode, Componente1.D5_PWM
  N3: Componente1.A0, Part6.AO
  N4: Componente1.D8, KY-2.ground
  GND: Componente1.GND, R1.Pin_1, R2.Pin_1, R3.Pin_1, S2.Pin_3, S2.Pin_4, U2.GND, U2.TXD, LCM1602_IIC2.GND, Tiny_RTC2.GND#10, Part6.GND, S3.Pin_3, S3.Pin_4, S4.Pin_3, S4.Pin_4, KY-2.power
  3V3: Componente1.D0/RX, Componente1.3V3, U2.RXD, U2.VCC
  N5: Componente1.D2, S4.Pin_1, S4.Pin_2
  N6: Componente1.D3_PWM, S3.Pin_1, S3.Pin_2
  N7: Componente1.D4, S2.Pin_1, S2.Pin_2
  N8: Componente1.D6_PWM, LED1.anode
  N9: Componente1.D7, LED3.anode
  5V: Componente1.5V, Part6.VCC
  N10: R1.Pin_0, LED1.cathode
  N11: LED3.cathode, R3.Pin_0
  VSS: LCD1.VSS, LCM1602_IIC2.VSS
  VDD: LCD1.VDD, LCM1602_IIC2.VDD
  N12: LCD1.V0, LCM1602_IIC2.V0
  N13: LCD1.RS, LCM1602_IIC2.RS
  N14: LCD1.R/W, LCM1602_IIC2.RW
  N15: LCD1.E, LCM1602_IIC2.E
  N16: LCD1.DB0, LCM1602_IIC2.D0
  N17: LCD1.DB1, LCM1602_IIC2.D1
  N18: LCD1.DB2, LCM1602_IIC2.D2
  N19: LCD1.DB3, LCM1602_IIC2.D3
  N20: LCD1.DB4, LCM1602_IIC2.D4
  N21: LCD1.DB5, LCM1602_IIC2.D5
  N22: LCD1.DB6, LCM1602_IIC2.D6
  N23: LCD1.DB7, LCM1602_IIC2.D7
  N24: LCD1.LED+, LCM1602_IIC2.A
  N25: LCD1.LED-, LCM1602_IIC2.K
  N26: U2.GPIO_0, U2.RST
  N27: U2.GPIO_2, U2.CH_PD
  N28: LCM1602_IIC2.VCC, LCM1602_IIC2.SDA, LCM1602_IIC2.SCL, Tiny_RTC2.VCC#9, Tiny_RTC2.BAT, KY-2.signal
  N29: LCM1602_IIC2.LED_A, LCM1602_IIC2.LED_B
  N30: Part6.POS, Part7.POS
  N31: Part6.NEG, Part7.NEG
  N32: VALVE2.no_name_yet#1, Power_plug1.VCC
  N33: VALVE2.no_name_yet#2, KY-2.C
  N34: Power_plug1.GND, KY-2.NO

notes:
  [ Motor de Pivô de Irrigação]
  [Bomba de Irrigação]
  [Fonte de energia]

custom parts:
  ESP8266 WiFi Module: Generic WiFi Module based on the ESP8266 with onboard PCB antenna and UART communications
  LCM1602 IIC: I2C-Module to use a 1602 or 2004 LCD on with the wire.h libory Serial LCD Modul
  Tiny RTC: Tiny RTC I2C module DS1370Z RTC and AT24C32 EEPROM
  FC-28 Soil Hygrometer Module: The FC-28 is a soil hygrometer module that uses the Texas Instruments LM393 comparator chip to provide an analog measurement of soil humidity. The digital output is high when soil moisture is over a certain threshold, as determined by adjusting the potentiometer.
  FC-28 Soil Hygrometer Module - Probe: The FC-28 is a soil hygrometer module that uses the Texas Instruments LM393 comparator chip to provide an analog measurement of soil humidity.
  Keyes Relay: The Keyes 5V relay module is suitable for SCM development, home appliance control. It uses a 5V~12V TIL control signal which can control DC / AC signal.
